# Fritzing sketch RC-Araba-Alıcı (saved by Fritzing 0.9.6b)
circuit board: 8.46667cm x 5.64444cm

parts:
  Parça1 = Arduino Nano (Rev3.0)
  L298N1 = L298N DC motor driver
  Parça3 = NRF24L01+ Breakout Board
  BAT1 = Battery Holders [package=battery-aaa]
  Parça4 = Arduino Nano (Rev3.0)
  J1 = Camdenboss CTB0158-3 [part_number=CTB0158-3 package=THT]
  J2 = Camdenboss CTB0158-4 [part_number=CTB0158-4 package=THT]
  J3 = Camdenboss CTB0158-2 [part_number=CTB0158-2 package=THT]
  J4 = Camdenboss CTB0158-3 [part_number=CTB0158-3 package=THT]
  J5 = Camdenboss CTB0158-2 [part_number=CTB0158-2 package=THT]
  J6 = Camdenboss CTB0158-3 [part_number=CTB0158-3 package=THT]
  J7 = Camdenboss CTB0158-3 [part_number=CTB0158-3 package=THT]
  J8 = Camdenboss CTB0158-3 [part_number=CTB0158-3 package=THT]

nets:
  GND: Parça1.GND, L298N1.GND, Parça3.GND
  N1: Parça1.D2, L298N1.IN4
  N2: Parça1.D3, L298N1.ENB
  N3: Parça1.D4, L298N1.IN3
  N4: Parça1.D5, L298N1.IN2
  N5: Parça1.D6, L298N1.ENA
  N6: Parça1.D7, L298N1.IN1
  N7: Parça1.D9, Parça3.CE
  N8: Parça1.D10, Parça3.CS
  N9: Parça1.D11/MOSI, Parça3.MOSI
  N10: Parça1.D12/MISO, Parça3.MISO
  3V3: Parça1.3V3, Parça3.VCC
  N11: Parça1.D13/SCK, Parça3.SCK
  N12: L298N1.12V, BAT1.+
  N13: Parça4.GND, J3.pin1, J3.pin2, J8.pin2
  N14: Parça4.D2, J4.pin2
  N15: Parça4.D3, J4.pin3
  N16: Parça4.D4, J4.pin1
  N17: Parça4.D5, J1.pin3
  N18: Parça4.D6, J1.pin1
  N19: Parça4.D7, J1.pin2
  N20: Parça4.D9, J2.pin4
  N21: Parça4.D10, J2.pin3
  N22: Parça4.D11/MOSI, J2.pin2
  N23: Parça4.D12/MISO, J2.pin1
  N24: Parça4.VIN, J8.pin1
  N25: Parça4.5V, J8.pin3
  N26: Parça4.A6, J7.pin1
  N27: Parça4.A4, J7.pin2
  N28: Parça4.A3, J7.pin3
  N29: Parça4.A2, J6.pin1
  N30: Parça4.A1, J6.pin2
  N31: Parça4.A0, J6.pin3
  N32: Parça4.3V3, J5.pin1
  N33: Parça4.D13/SCK, J5.pin2

notes:
  12v kadar Amperli şarj edilebilir bir pil olsun.
  Ara adaptör kullanmıyorsan (üzerinde 8 GİRİŞ olan bir adaptör) sakın 5V gönderme. 3V olmalı. Ama adaptör varsa o zaten süşürüyor.
  VCC-CSE-MOSI-IRQ
  GND-CE-SCK-MISO

custom parts:
  L298N DC motor driver: 2x DC motor driver with 78M05 positive voltage regulator (7..35 V) L298N: max 46 V, 2 A Set 5 V Enable jumper to enable 5 V regultor (needed for the L298N) and +5 V output at screw terminal or supply external +5 V at screw terminal Set ENA and/or ENB to +5 V to enable motor permanently or supply ENA and/or ENB with PWM signal IN1 and IN2 set rotation directory for motor A (OUT1/OUT2) IN2 and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
