# Fritzing sketch RC-Araba-Verici (saved by Fritzing 0.9.6b)

parts:
  Parça4 = Arduino Nano (Rev3.0)
  Parça6 = NRF24L01+ Breakout Board
  BAT2 = Battery Holders [package=battery-aaa]
  Parça7 = Thumb Joystick

nets:
  GND: Parça4.GND, Parça6.GND, BAT2.-
  N1: Parça4.D9, Parça6.CE
  N2: Parça4.D10, Parça6.CS
  N3: Parça4.D11/MOSI, Parça6.MOSI
  N4: Parça4.D12/MISO, Parça6.MISO
  N5: Parça4.VIN, BAT2.+
  5V: Parça4.5V, Parça7.VCC
  N6: Parça4.A1, Parça7.VERT
  N7: Parça4.A0, Parça7.HORZ
  3V3: Parça4.3V3, Parça6.VCC
  N8: Parça4.D13/SCK, Parça6.SCK

notes:
  12v kadar Amperli şarj edilebilir bir pil olsun.
  Ara adaptör kullanmıyorsan (üzerinde 8 GİRİŞ olan bir adaptör) sakın 5V gönderme. 3V olmalı. Ama adaptör varsa o zaten süşürüyor.
  VCC-CSE-MOSI-IRQ
  GND-CE-SCK-MISO
